// Logisim project alu.circ as structural Verilog: 5 circuits, main circuit main
module main (
  input  [15:0] X,
  input  [15:0] Y,
  input  [3:0] Switch__S,
  output Signed_Overflow,
  output [15:0] RESULT,
  output Equal
);

  wire add_overflow_1_out, addp8_overflow_1_out, comparator_1_lt, sub_overflow_1_out, subp8_overflow_1_out;
  wire [15:0] Add, addp8, And, Or, SLLV, SLT, SRAV, SRLV, Sub, subp8;

  Subtractor #(.width(16)) subtractor_1 (.a(X), .b(Y), .out(Sub));  // open: bin, bout
  Shifter #(.width(16)) shifter_1 (.in(X), .\dist (Y[3:0]), .out(SLLV));
  Shifter #(.width(16), .shift("lr")) shifter_2 (.in(X), .\dist (Y[3:0]), .out(SRLV));
  Shifter #(.width(16), .shift("ar")) shifter_3 (.in(X), .\dist (Y[3:0]), .out(SRAV));
  Adder #(.width(16)) adder_1 (.a(X), .b(Y), .out(Add));  // open: cin, cout
  Comparator #(.width(16)) comparator_1 (.a(X), .b(Y), .lt(comparator_1_lt));  // open: gt, eq
  assign And = X & Y;  // AND_Gate and_1, 16 bits wide
  Multiplexer #(.width(16)) multiplexer_1 (
    .in0({16{1'b0}}), .in1(16'h1), .out(SLT), .sel(comparator_1_lt));  // open: en
  Multiplexer #(.select(4), .width(16)) multiplexer_2 (
    .in0(Add), .in1(Sub), .in2(SLLV), .in3(SRLV), .in4(SRAV), .in5(SLT), .in6(Or), .in7(And), .in8(addp8),
    .in9(subp8), .out(RESULT), .sel(Switch__S));  // open: in10, in11, in12, in13, in14, in15, en
  assign Or = X | Y;  // OR_Gate or_1, 16 bits wide
  addp8_overflow addp8_overflow_1 (.X(X), .Y(Y), .out(addp8_overflow_1_out));
  Add_Overflow add_overflow_1 (.in_1(X), .in_2(Y), .out(add_overflow_1_out));
  Sub_Overflow sub_overflow_1 (.in_1(X), .in_2(Y), .out(sub_overflow_1_out));
  Multiplexer #(.select(4)) multiplexer_3 (
    .in0(add_overflow_1_out), .in1(sub_overflow_1_out), .in8(addp8_overflow_1_out),
    .in9(subp8_overflow_1_out), .out(Signed_Overflow), .sel(Switch__S));  // open: in2, in3, in4, in5, in6, in7, in10, in11, in12, in13, in14, in15, en
  subp8_overflow subp8_overflow_1 (.X(X), .Y(Y), .out(subp8_overflow_1_out));
  Comparator #(.width(16)) comparator_2 (.a(X), .b(Y), .eq(Equal));  // open: gt, lt
  Subtractor subtractor_2 (.a(X[15:8]), .b(Y[15:8]), .out(subp8[15:8]));  // open: bin, bout
  Subtractor subtractor_3 (.a(X[7:0]), .b(Y[7:0]), .out(subp8[7:0]));  // open: bin, bout
  Adder adder_2 (.a(X[15:8]), .b(Y[15:8]), .out(addp8[15:8]));  // open: cin, cout
  Adder adder_3 (.a(X[7:0]), .b(Y[7:0]), .out(addp8[7:0]));  // open: cin, cout

  // Other names for the same wires on the sheet: Selec[3:0] = Switch__S

  // Notes on the sheet:
  //   INPUTS to your circuit
  //   INPUT to your circuit
  //   DON'T CHANGE THE INPUTS AND OUTPUTS! IF YOU DO SO, YOU NEED TO MAKE SURE THE PINS ARE IN THE RIGHT PLACES!
  //   OUTPUTS of your circuit
endmodule

module Add_Overflow (
  input  [15:0] in_1,
  input  [15:0] in_2,
  output out
);

  wire Add, and_1_out, and_2_out;
  wire [14:0] adder_1_out;

  Adder #(.width(16)) adder_1 (.a(in_1), .b(in_2), .out({Add, adder_1_out}));  // open: cin, cout
  and and_1 (and_1_out, ~in_1[15], Add, ~in_2[15]);  // AND_Gate
  and and_2 (and_2_out, in_1[15], ~Add, in_2[15]);  // AND_Gate
  or or_1 (out, and_1_out, and_2_out);

  // Other names for the same wires on the sheet: X = in_1[15]; Y = in_2[15]
endmodule

module Sub_Overflow (
  input  [15:0] in_1,
  input  [15:0] in_2,
  output out
);

  wire and_1_out, and_2_out, Sub;
  wire [14:0] subtractor_1_out;

  Subtractor #(.width(16)) subtractor_1 (.a(in_1), .b(in_2), .out({Sub, subtractor_1_out}));  // open: bin, bout
  and and_1 (and_1_out, ~in_1[15], Sub, in_2[15]);  // AND_Gate
  and and_2 (and_2_out, in_1[15], ~Sub, ~in_2[15]);  // AND_Gate
  or or_1 (out, and_1_out, and_2_out);

  // Other names for the same wires on the sheet: X = in_1[15]; Y = in_2[15]
endmodule

module subp8_overflow (
  input  [15:0] X,
  input  [15:0] Y,
  output out
);

  wire and_1_out, and_2_out, and_3_out, and_4_out, Bottom, Top;
  wire [6:0] subtractor_1_out, subtractor_2_out;

  Subtractor subtractor_1 (.a(X[15:8]), .b(Y[15:8]), .out({Top, subtractor_1_out}));  // open: bin, bout
  Subtractor subtractor_2 (.a(X[7:0]), .b(Y[7:0]), .out({Bottom, subtractor_2_out}));  // open: bin, bout
  and and_1 (and_1_out, ~X[15], Top, Y[15]);  // AND_Gate
  and and_2 (and_2_out, ~X[7], Bottom, Y[7]);  // AND_Gate
  and and_3 (and_3_out, X[7], ~Bottom, ~Y[7]);  // AND_Gate
  and and_4 (and_4_out, X[15], ~Top, ~Y[15]);  // AND_Gate
  or or_1 (out, and_1_out, and_2_out, and_3_out, and_4_out);

  // Other names for the same wires on the sheet: X_bot = X[7]; X_top = X[15]; Y_bot = Y[7]; Y_top = Y[15]
endmodule

module addp8_overflow (
  input  [15:0] X,
  input  [15:0] Y,
  output out
);

  wire and_1_out, and_2_out, and_3_out, and_4_out, Bottom, Top;
  wire [6:0] adder_1_out, adder_2_out;

  Adder adder_1 (.a(X[15:8]), .b(Y[15:8]), .out({Top, adder_1_out}));  // open: cin, cout
  Adder adder_2 (.a(X[7:0]), .b(Y[7:0]), .out({Bottom, adder_2_out}));  // open: cin, cout
  and and_1 (and_1_out, ~X[15], Top, ~Y[15]);  // AND_Gate
  and and_2 (and_2_out, ~X[7], ~Y[7]);  // AND_Gate
  and and_3 (and_3_out, X[7], ~Bottom, Y[7]);  // AND_Gate
  and and_4 (and_4_out, X[15], ~Top, Y[15]);  // AND_Gate
  or or_1 (out, and_1_out, and_2_out, and_3_out, and_4_out);

  // Other names for the same wires on the sheet: X_bot = X[7]; X_top = X[15]; Y_bot = Y[7]; Y_top = Y[15]
endmodule
