// Logisim project cpu.circ as structural Verilog: 3 circuits, main circuit main
module main (
  input  [15:0] From_Instr_Mem,
  input  clk,
  output [15:0] r0,
  output [15:0] r1,
  output [15:0] r2,
  output [15:0] r3,
  output [15:0] Display_0,
  output [15:0] Display_1,
  output [15:0] To_Instr_Mem,
  output [15:0] Data_Mem_Data,
  output [15:0] Data_Mem_Addr,
  output Data_Mem_Write
);

  wire and_1_out, and_2_out, and_3_out, and_4_out, and_5_out, beq, bne, branch, button_1_out,
       comparator_1_eq, comparator_2_eq, display, equals, Itype, jr, jump, lui, main_2_signed_overflow,
       Mem2Reg, nop, not_1_out, or_1_out, Rtype, \signed , Write2Reg;
  wire [1:0] multiplexer_2_out, multiplexer_3_out, rd, rs, rt;
  wire [3:0] multiplexer_11_out, opcode, switch;
  wire [5:0] funct;
  wire [7:0] imm;
  wire [11:0] target_addr;
  wire [15:0] adder_1_out, adder_2_out, aluread1, and_6_out, bit_extender_1_out, bit_extender_2_out,
       bit_extender_3_out, DataOut, immediate, multiplexer_1_out, multiplexer_5_out, multiplexer_6_out,
       multiplexer_7_out, multiplexer_8_out, multiplexer_9_out, multiplexer_10_out, multiplexer_12_out,
       multiplexer_13_out, multiplexer_14_out, multiplexer_15_out, or_3_out, register_1_q, shifter_1_out;

  Multiplexer #(.width(16), .enable("false")) multiplexer_1 (
    .in0(From_Instr_Mem), .in1(16'h6), .out(multiplexer_1_out), .sel(nop));
  assign bit_extender_1_out = {{8{1'b0}}, imm};  // Bit_Extender bit_extender_1
  assign bit_extender_2_out = {{8{imm[7]}}, imm};  // Bit_Extender bit_extender_2
  Register #(.width(16)) register_1 (.D(multiplexer_1_out), .Q(register_1_q), .clk(clk));  // open: en, clr
  Regfile_main main_1 (
    .Read_register_1(rs), .Read_register_2(rt), .write_register(multiplexer_2_out),
    .write_data(multiplexer_7_out), .Reg_0_Value(r0), .Reg_1_Value(r1), .Reg_2_Value(r2), .Reg_3_Value(r3),
    .RegWrite(Write2Reg), .clock(clk), .Read_Data_1(aluread1), .Read_Data_2(Data_Mem_Data));
  Multiplexer #(.width(2)) multiplexer_2 (
    .in0(multiplexer_3_out), .in1(2'b11), .out(multiplexer_2_out), .sel(jump));  // open: en
  instructions instructions_1 (
    .instructions(register_1_q), .\function (funct), .target_add(target_addr), .op(opcode), .immediate(imm),
    .rd(rd), .rt(rt), .rs(rs));
  Multiplexer #(.width(2)) multiplexer_3 (.in0(rt), .in1(rd), .out(multiplexer_3_out), .sel(Rtype));  // open: en
  Multiplexer #(.width(16), .enable("false")) multiplexer_4 (
    .in0(bit_extender_1_out), .in1(bit_extender_2_out), .out(immediate), .sel(\signed ));
  Shifter #(.width(16)) shifter_1 (.in(immediate), .\dist (4'b1000), .out(shifter_1_out));
  Multiplexer #(.width(16)) multiplexer_5 (
    .in0(Data_Mem_Addr), .in1(DataOut), .out(multiplexer_5_out), .sel(Mem2Reg));  // open: en
  Comparator #(.width(16)) comparator_1 (.a(immediate), .b({16{1'b0}}), .eq(comparator_1_eq));  // open: gt, lt
  Register #(.width(16)) register_2 (.D(multiplexer_15_out), .Q(To_Instr_Mem), .clk(clk));  // open: en, clr
  Multiplexer #(.width(16)) multiplexer_6 (
    .in0(multiplexer_5_out), .in1(shifter_1_out), .out(multiplexer_6_out), .sel(lui));  // open: en
  Multiplexer #(.width(16)) multiplexer_7 (
    .in0(multiplexer_6_out), .in1(To_Instr_Mem), .out(multiplexer_7_out), .sel(jump));  // open: en
  Hex_Digit_Display hex_digit_display_1 (.value(Display_0[11:8]));  // open: dp
  Hex_Digit_Display hex_digit_display_2 (.value(Display_0[15:12]));  // open: dp
  Multiplexer #(.width(16)) multiplexer_8 (
    .in0(Display_0), .in1(aluread1), .out(multiplexer_8_out), .sel(and_1_out));  // open: en
  and and_1 (and_1_out, comparator_1_eq, display);
  Hex_Digit_Display hex_digit_display_3 (.value(Display_0[3:0]));  // open: dp
  Hex_Digit_Display hex_digit_display_4 (.value(Display_0[7:4]));  // open: dp
  Register #(.width(16)) register_3 (.D(multiplexer_8_out), .Q(Display_0), .clk(clk));  // open: en, clr
  Adder #(.width(16)) adder_1 (.a(To_Instr_Mem), .b(16'h1), .out(adder_1_out));  // open: cin, cout
  and and_2 (and_2_out, or_1_out, branch);
  or or_1 (or_1_out, and_4_out, and_3_out);
  and and_3 (and_3_out, bne, ~equals);  // AND_Gate
  and and_4 (and_4_out, beq, equals);
  Multiplexer #(.width(16)) multiplexer_9 (
    .in0(adder_1_out), .in1(To_Instr_Mem), .out(multiplexer_9_out), .sel(and_2_out));  // open: en
  or or_2 (nop, and_2_out, jump);
  Multiplexer #(.width(16)) multiplexer_10 (
    .in0(Data_Mem_Data), .in1(immediate), .out(multiplexer_10_out), .sel(Itype));  // open: en
  Hex_Digit_Display hex_digit_display_5 (.value(Display_1[11:8]));  // open: dp
  Hex_Digit_Display hex_digit_display_6 (.value(Display_1[15:12]));  // open: dp
  and and_5 (and_5_out, comparator_2_eq, display);
  Comparator #(.width(16)) comparator_2 (.a(immediate), .b(16'h1), .eq(comparator_2_eq));  // open: gt, lt
  Adder #(.width(16)) adder_2 (.a(multiplexer_9_out), .b(immediate), .out(adder_2_out));  // open: cin, cout
  assign bit_extender_3_out = {{4{1'b0}}, target_addr};  // Bit_Extender bit_extender_3
  LED led_1 (.in(main_2_signed_overflow));
  alu_main main_2 (
    .Switch__S(multiplexer_11_out), .X(aluread1), .Equal(equals), .RESULT(Data_Mem_Addr),
    .Signed_Overflow(main_2_signed_overflow), .Y(multiplexer_10_out));
  Multiplexer #(.width(4)) multiplexer_11 (
    .in0(switch), .in1(funct[3:0]), .out(multiplexer_11_out), .sel(Rtype));  // open: en
  Hex_Digit_Display hex_digit_display_7 (.value(Display_1[7:4]));  // open: dp
  Hex_Digit_Display hex_digit_display_8 (.value(Display_1[3:0]));  // open: dp
  Register #(.width(16)) register_4 (.D(multiplexer_12_out), .Q(Display_1), .clk(clk));  // open: en, clr
  Multiplexer #(.width(16)) multiplexer_12 (
    .in0(Display_1), .in1(aluread1), .out(multiplexer_12_out), .sel(and_5_out));  // open: en
  Multiplexer #(.width(16)) multiplexer_13 (
    .in0(multiplexer_9_out), .in1(adder_2_out), .out(multiplexer_13_out), .sel(and_2_out));  // open: en
  Multiplexer #(.width(16)) multiplexer_14 (
    .in0(multiplexer_13_out), .in1(or_3_out), .out(multiplexer_14_out), .sel(jump));  // open: en
  assign or_3_out = bit_extender_3_out | and_6_out;  // OR_Gate or_3, 16 bits wide
  assign and_6_out = 16'hf000 & To_Instr_Mem;  // AND_Gate and_6, 16 bits wide
  Multiplexer #(.width(16)) multiplexer_15 (
    .in0(multiplexer_14_out), .in1(aluread1), .out(multiplexer_15_out), .sel(jr));  // open: en
  assign DataOut = Data_Mem_Write ? Data_Mem_Data : 16'bz;  // Controlled_Buffer controlled_buffer_1
  not not_1 (not_1_out, Data_Mem_Write);
  RAM #(.addrWidth(16), .dataWidth(16)) ram_1 (
    .addr(Data_Mem_Addr), .data(DataOut), .sel(1'b1), .clk(clk), .ld(not_1_out), .clr(button_1_out));
  Button button_1 (.out(button_1_out));
  control control_1 (
    .op(opcode), .Rtype(Rtype), .bne(bne), .beq(beq), .jump(jump), .jr(jr), .lui(lui), .Mem2Reg(Mem2Reg),
    .MemWrite(Data_Mem_Write), .display(display), .imm(Itype), .Write2Reg(Write2Reg), .\signed (\signed ),
    .branch(branch), .signControl(switch));

  // Other names for the same wires on the sheet: aluread2[15:0] = Data_Mem_Data; d0[15:0] = Display_0;
  //   d1[15:0] = Display_1; DMemAdd[15:0] = Data_Mem_Addr; InstrMem[15:0] = From_Instr_Mem; MemWrite = Data_Mem_Write;
  //   PC[15:0] = To_Instr_Mem

  // Notes on the sheet:
  //   Clock
  //   This is the current PC that you need to send as OUTPUT
  //   This is the instruction that you would receive as INPUT
  //   Given
  //   Instruction
  //   This is a CLK that is an INPUT driven from the harness.
  //   Remember, this circuit is loaded from the harness to be tested!
  //   DO NOT CHANGE THE LOCATIONS OF THE INPUTS OR OUTPUTS! IF YOU DO SO, YOU NEED TO MAKE SURE THE PINS ARE IN THE RIGHT PLACES!
  //   Write
  //   These are OUTPUTS of the circuit
  //   Display
  //   ALU
  //   Datapath
  //   Control
  //   These are OUTPUTS of the circuit
  //   Memory
endmodule

module instructions (
  input  [15:0] instructions,
  output [5:0] \function ,
  output [7:0] immediate,
  output [1:0] rd,
  output [1:0] rt,
  output [1:0] rs,
  output [3:0] op,
  output [11:0] target_add
);


  assign \function  = instructions[5:0];
  assign immediate = instructions[7:0];
  assign op = instructions[15:12];
  assign rd = instructions[7:6];
  assign rs = instructions[11:10];
  assign rt = instructions[9:8];
  assign target_add = instructions[11:0];
endmodule

module control (
  input  [3:0] op,
  output Rtype,
  output bne,
  output beq,
  output jump,
  output jr,
  output lui,
  output Mem2Reg,
  output MemWrite,
  output display,
  output imm,
  output Write2Reg,
  output \signed ,
  output branch,
  output [3:0] signControl
);

  wire addi, andi, j, jal, ori;
  wire [3:0] multiplexer_2_out, multiplexer_3_out;

  or or_1 (jump, j, jr, jal);
  Demultiplexer #(.select(4), .enable("false")) demultiplexer_1 (
    .out0(Rtype), .out1(jal), .out2(j), .out3(jr), .out4(beq), .out5(addi), .out6(andi), .out7(ori),
    .out8(bne), .out9(MemWrite), .out10(lui), .out11(Mem2Reg), .out12(display), .in(1'b1), .sel(op));  // open: out13, out14, out15
  or or_2 (imm, ori, andi, addi, Mem2Reg, MemWrite);
  or or_3 (Write2Reg, jal, addi, andi, lui, ori, Mem2Reg, Rtype);
  or or_4 (\signed , beq, MemWrite, Mem2Reg, addi, bne);
  or or_5 (branch, beq, bne);
  Multiplexer #(.width(4)) multiplexer_1 (
    .in0(multiplexer_2_out), .in1(4'b0110), .out(signControl), .sel(ori));  // open: en
  Multiplexer #(.width(4)) multiplexer_2 (
    .in0(multiplexer_3_out), .in1(4'b1111), .out(multiplexer_2_out), .sel(lui));  // open: en
  Multiplexer #(.width(4)) multiplexer_3 (
    .in0(4'b0000), .in1(4'b0111), .out(multiplexer_3_out), .sel(andi));  // open: en

  // Other names for the same wires on the sheet: disp = display; lw = Mem2Reg; sw = MemWrite

  // Notes on the sheet:
  //   single cycle cpu lecture
endmodule
